// Logisim project Cache.circ as structural Verilog: 3 circuits, main circuit implementation
module implementation (
  input  [9:0] CpuAddressIn,
  input  CpuReadIn,
  input  CpuWriteIn,
  input  [7:0] CpuWriteValueIn,
  input  [31:0] LineFromMemIn,
  input  ClkIn,
  output ReadyOut,
  output DidContainOut,
  output [7:0] ByteReadOut,
  output [7:0] MemAddressOut,
  output MemReadOut,
  output MemWriteOut,
  output [31:0] Line2MemOut
);

  wire and_1_out, and_2_out, and_3_out, and_4_out, and_5_out, and_6_out, and_7_out, and_8_out, and_9_out,
       and_10_out, and_11_out, and_12_out, and_13_out, and_14_out, and_17_out, and_18_out, and_19_out,
       and_20_out, and_21_out, and_22_out, and_23_out, and_24_out, and_25_out, and_27_out, contains0,
       contains1, ContainsValue, CpuRead, CpuWrite, demultiplexer_6_out0, demultiplexer_6_out1,
       EnableWayWrite, EnableWayWrite0, EnableWayWrite1, InitializeAge, InitializeAge0, InitializeAge1,
       not_1_out, not_2_out, not_3_out, not_4_out, not_5_out, not_6_out, not_7_out, not_8_out, not_9_out,
       not_10_out, not_11_out, not_12_out, not_13_out, OlderTagDirty, OlderTagDirty0, OlderTagDirty1, Reset,
       S0, S1, S2, undriven, undriven_2, undriven_3, WriteFrom;
  wire [1:0] Offsetbits_set0, Offsetbits_set1;
  wire [2:0] or_1_out;
  wire [6:0] multiplexer_7_out, OlderTag0, OlderTag1, Tagbits_set0, Tagbits_set1;
  wire [7:0] ByteReadOut0, ByteReadOut1, CpuWriteValue, CPUWriteValue0, CPUWriteValue1;
  wire [9:0] CpuAddress;
  wire [31:0] Blockedmem_set0, Blockedmem_set1, OlderBlock0, OlderBlock1;

  Register #(.width(1)) register_1 (.D(CpuReadIn), .en(ReadyOut), .clk(ClkIn), .Q(CpuRead), .clr(undriven));
  Register #(.width(1)) register_2 (.D(CpuWriteIn), .en(ReadyOut), .clk(ClkIn), .Q(CpuWrite), .clr(undriven_2));
  Register register_3 (.D(CpuWriteValueIn), .en(ReadyOut), .clk(ClkIn), .Q(CpuWriteValue), .clr(undriven_3));
  Register #(.width(10)) register_4 (.D(CpuAddressIn), .en(ReadyOut), .clk(ClkIn), .Q(CpuAddress));  // open: clr
  not not_1 (not_1_out, CpuRead);
  not not_2 (not_2_out, CpuWrite);
  not not_3 (not_3_out, ContainsValue);
  not not_4 (not_4_out, OlderTagDirty);
  not not_5 (not_5_out, S2);
  not not_6 (not_6_out, S1);
  not not_7 (not_7_out, S0);
  and and_1 (and_1_out, not_7_out, not_6_out);
  and and_2 (and_2_out, not_7_out, not_1_out, CpuWrite, OlderTagDirty);
  and and_3 (and_3_out, not_7_out, not_1_out, CpuWrite, ContainsValue);
  and and_4 (and_4_out, not_7_out, CpuRead, not_2_out, OlderTagDirty);
  and and_5 (and_5_out, not_7_out, CpuRead, not_2_out, ContainsValue);
  and and_6 (and_6_out, not_5_out, S0);
  and and_7 (and_7_out, S1, not_7_out);
  and and_8 (and_8_out, S2, not_7_out);
  and and_9 (and_9_out, S1, not_5_out, S0);
  and and_10 (and_10_out, S1, S2, not_1_out);
  and and_11 (and_11_out, not_5_out, S1, CpuRead, not_2_out, not_4_out);
  and and_12 (and_12_out, not_5_out, S1, CpuRead, not_2_out, ContainsValue);
  and and_13 (and_13_out, S1, not_1_out, CpuWrite, not_4_out);
  and and_14 (and_14_out, S1, not_1_out, CpuWrite, ContainsValue);
  or or_1 (or_1_out[0], and_1_out, and_2_out, and_3_out, and_4_out, and_5_out, S2);
  or or_2 (or_1_out[1], and_6_out, and_7_out);
  or or_3 (or_1_out[2], and_8_out, and_9_out, and_10_out, and_11_out, and_12_out, and_13_out, and_14_out);
  Register #(.width(3)) register_5 (.D(or_1_out), .clk(ClkIn), .Q({S2, S1, S0}));  // open: en, clr
  not not_8 (not_8_out, DidContainOut);
  not not_9 (not_9_out, S2);
  not not_10 (not_10_out, S1);
  not not_11 (not_11_out, S0);
  and and_15 (Reset, not_9_out, not_10_out, not_11_out);
  and and_16 (ReadyOut, not_9_out, not_10_out, S0);
  and and_17 (and_17_out, S2, S1, CpuRead, not_11_out, not_2_out, not_8_out);
  and and_18 (and_18_out, S2, S1, CpuWrite, not_11_out, not_1_out, not_8_out);
  and and_19 (and_19_out, not_9_out, not_8_out, not_1_out, S1, S0, CpuWrite, OlderTagDirty);
  and and_20 (and_20_out, not_9_out, not_8_out, not_2_out, S1, S0, CpuRead, OlderTagDirty);
  and and_21 (and_21_out, S2, S0, CpuWrite, not_10_out, not_1_out);
  and and_22 (and_22_out, S2, S1, CpuWrite, not_11_out, not_1_out, not_8_out);
  and and_23 (and_23_out, S2, S1, CpuRead, not_11_out, not_2_out, not_8_out);
  and and_24 (and_24_out, S0, S1, S2);
  and and_25 (and_25_out, not_9_out, not_10_out, not_11_out);
  and and_26 (WriteFrom, S2, S0, CpuWrite, not_10_out, not_1_out);
  or or_4 (MemReadOut, and_17_out, and_18_out);
  or or_5 (MemWriteOut, and_19_out, and_20_out);
  or or_6 (EnableWayWrite, and_21_out, and_22_out, and_23_out);
  or or_7 (InitializeAge, and_24_out, and_25_out);
  Demultiplexer #(.enable("false"), .width(7)) demultiplexer_1 (
    .out0(Tagbits_set0), .out1(Tagbits_set1), .in(CpuAddress[9:3]), .sel(CpuAddress[2]));
  Demultiplexer #(.enable("false"), .width(2)) demultiplexer_2 (
    .out0(Offsetbits_set0), .out1(Offsetbits_set1), .in(CpuAddress[1:0]), .sel(CpuAddress[2]));
  Demultiplexer #(.enable("false"), .width(32)) demultiplexer_3 (
    .out0(Blockedmem_set0), .out1(Blockedmem_set1), .in(LineFromMemIn), .sel(CpuAddress[2]));
  Demultiplexer #(.enable("false"), .width(8)) demultiplexer_4 (
    .out0(CPUWriteValue0), .out1(CPUWriteValue1), .in(CpuWriteValue), .sel(CpuAddress[2]));
  Demultiplexer #(.enable("false")) demultiplexer_5 (
    .out0(EnableWayWrite0), .out1(EnableWayWrite1), .in(EnableWayWrite), .sel(CpuAddress[2]));
  Demultiplexer #(.enable("false")) demultiplexer_6 (
    .out0(demultiplexer_6_out0), .out1(demultiplexer_6_out1), .in(InitializeAge), .sel(CpuAddress[2]));
  Multiplexer #(.enable("false")) multiplexer_1 (
    .in0(demultiplexer_6_out1), .in1(1'b1), .out(InitializeAge0), .sel(Reset));
  Multiplexer #(.enable("false")) multiplexer_2 (
    .in0(demultiplexer_6_out0), .in1(1'b1), .out(InitializeAge1), .sel(Reset));
  Set Set0 (
    .InitIn(Reset), .Tag(Tagbits_set0), .Offset(Offsetbits_set0), .BlockMem(Blockedmem_set0),
    .Value(CPUWriteValue0), .Write(WriteFrom), .WayWrite(EnableWayWrite0), .NewAges(InitializeAge0),
    .ClkIn(ClkIn), .contain(contains0), .OlderTagOut(OlderTag0), .OlderTagDirtyOut(OlderTagDirty0),
    .ByteReadOut(ByteReadOut0), .OlderBlockOut(OlderBlock0));
  Set Set1 (
    .InitIn(Reset), .Tag(Tagbits_set1), .Offset(Offsetbits_set1), .BlockMem(Blockedmem_set1),
    .Value(CPUWriteValue1), .Write(WriteFrom), .WayWrite(EnableWayWrite1), .NewAges(InitializeAge1),
    .ClkIn(ClkIn), .contain(contains1), .OlderTagOut(OlderTag1), .OlderTagDirtyOut(OlderTagDirty1),
    .ByteReadOut(ByteReadOut1), .OlderBlockOut(OlderBlock1));
  Multiplexer #(.enable("false")) multiplexer_3 (
    .in0(contains0), .in1(contains1), .out(ContainsValue), .sel(CpuAddress[2]));
  not not_12 (not_12_out, S2);
  not not_13 (not_13_out, S0);
  Register #(.width(1)) register_6 (.D(ContainsValue), .en(and_27_out), .clk(ClkIn), .Q(DidContainOut));  // open: clr
  and and_27 (and_27_out, not_12_out, S1, not_13_out);
  Multiplexer #(.enable("false"), .width(8)) multiplexer_4 (
    .in0(ByteReadOut0), .in1(ByteReadOut1), .out(ByteReadOut), .sel(CpuAddress[2]));
  Multiplexer #(.enable("false")) multiplexer_5 (
    .in0(OlderTagDirty0), .in1(OlderTagDirty1), .out(OlderTagDirty), .sel(CpuAddress[2]));
  Multiplexer #(.enable("false"), .width(32)) multiplexer_6 (
    .in0(OlderBlock0), .in1(OlderBlock1), .out(Line2MemOut), .sel(CpuAddress[2]));
  Multiplexer #(.enable("false"), .width(7)) multiplexer_7 (
    .in0(OlderTag0), .in1(OlderTag1), .out(multiplexer_7_out), .sel(CpuAddress[2]));
  Multiplexer #(.enable("false"), .select(2), .width(8)) multiplexer_8 (
    .in1({multiplexer_7_out, CpuAddress[2]}), .in2(CpuAddress[9:2]), .out(MemAddressOut),
    .sel({MemReadOut, MemWriteOut}));  // open: in0, in3

  // Other names for the same wires on the sheet: MemWrite = MemWriteOut; MemRead = MemReadOut; SetBit = CpuAddress[2];
  //   clk = ClkIn; OffsetBit[1:0] = CpuAddress[1:0]; TagBits[6:0] = CpuAddress[9:3]; DidContain = DidContainOut;
  //   LineFromMem[31:0] = LineFromMemIn; MemAddress[7:0] = MemAddressOut; Ready = ReadyOut;
  //   ByteRead[7:0] = ByteReadOut; SelectedSetByteRead[7:0] = ByteReadOut; Line2Mem[31:0] = Line2MemOut;
  //   SelectedSetLine2Mem[31:0] = Line2MemOut
endmodule

module Set (
  input  InitIn,
  input  [6:0] Tag,
  input  [1:0] Offset,
  input  [31:0] BlockMem,
  input  [7:0] Value,
  input  Write,
  input  WayWrite,
  input  NewAges,
  input  ClkIn,
  output contain,
  output [6:0] OlderTagOut,
  output OlderTagDirtyOut,
  output [7:0] ByteReadOut,
  output [31:0] OlderBlockOut
);

  wire contain0, contain1, contain2, DirtyWay0, DirtyWay1, DirtyWay2, WayWrite0, WayWrite1, WayWrite2;
  wire [1:0] adder_1_out, adder_2_out, adder_3_out, AgeWay0, AgeWay1, AgeWay2, Match, multiplexer_1_out,
       multiplexer_3_out, multiplexer_4_out, multiplexer_5_out, multiplexer_6_out, multiplexer_7_out,
       multiplexer_8_out, OldWay, WayAccessed, WayContains;
  wire [2:0] AgeCtr0, AgeCtr1, AgeCtr2, comparator_4_eq, comparator_7_eq;
  wire [6:0] WayTagOut0, WayTagOut1, WayTagOut2;
  wire [7:0] ByteReadOut0, ByteReadOut1, ByteReadOut2, Val0, Val1, Val2;
  wire [31:0] Block0, Block1, Block2, BlockIn0, BlockIn1, BlockIn2;

  Demultiplexer #(.enable("false"), .select(2), .width(32)) demultiplexer_1 (
    .out0(BlockIn0), .out1(BlockIn1), .out2(BlockIn2), .in(BlockMem), .sel(OldWay));  // open: out3
  Multiplexer #(.enable("false"), .width(2)) multiplexer_1 (
    .in0(OldWay), .in1(WayContains), .out(multiplexer_1_out), .sel(Write));
  Demultiplexer #(.enable("false"), .select(2), .width(8)) demultiplexer_2 (
    .out0(Val0), .out1(Val1), .out2(Val2), .in(Value), .sel(WayContains));  // open: out3
  Multiplexer #(.enable("false"), .select(2), .width(2)) multiplexer_2 (
    .in0(AgeWay0), .in1(AgeWay1), .in2(AgeWay2), .out(WayAccessed), .sel(WayContains));  // open: in3
  Demultiplexer #(.enable("false"), .select(2)) demultiplexer_3 (
    .out0(WayWrite0), .out1(WayWrite1), .out2(WayWrite2), .in(WayWrite), .sel(multiplexer_1_out));  // open: out3
  Comparator #(.mode("unsigned"), .width(2)) comparator_1 (
    .a(AgeWay0), .b(WayAccessed), .gt(AgeCtr0[0]), .eq(AgeCtr0[1]), .lt(AgeCtr0[2]));
  Comparator #(.mode("unsigned"), .width(2)) comparator_2 (
    .a(AgeWay1), .b(WayAccessed), .gt(AgeCtr1[0]), .eq(AgeCtr1[1]), .lt(AgeCtr1[2]));
  Comparator #(.mode("unsigned"), .width(2)) comparator_3 (
    .a(AgeWay2), .b(WayAccessed), .gt(AgeCtr2[0]), .eq(AgeCtr2[1]), .lt(AgeCtr2[2]));
  Adder #(.width(2)) adder_1 (.a(AgeWay0), .b(2'b01), .out(adder_1_out));  // open: cin, cout
  Adder #(.width(2)) adder_2 (.a(AgeWay1), .b(2'b01), .out(adder_2_out));  // open: cin, cout
  Adder #(.width(2)) adder_3 (.a(AgeWay2), .b(2'b01), .out(adder_3_out));  // open: cin, cout
  Multiplexer #(.enable("false"), .select(3), .width(2)) multiplexer_3 (
    .in1(AgeWay0), .in2(2'b00), .in4(adder_1_out), .out(multiplexer_3_out), .sel(AgeCtr0));  // open: in0, in3, in5, in6, in7
  Multiplexer #(.enable("false"), .select(3), .width(2)) multiplexer_4 (
    .in1(AgeWay1), .in2(2'b00), .in4(adder_2_out), .out(multiplexer_4_out), .sel(AgeCtr1));  // open: in0, in3, in5, in6, in7
  Multiplexer #(.enable("false"), .select(3), .width(2)) multiplexer_5 (
    .in1(AgeWay2), .in2(2'b00), .in4(adder_3_out), .out(multiplexer_5_out), .sel(AgeCtr2));  // open: in0, in3, in5, in6, in7
  Multiplexer #(.enable("false"), .width(2)) multiplexer_6 (
    .in0(multiplexer_3_out), .in1(2'b00), .out(multiplexer_6_out), .sel(InitIn));
  Multiplexer #(.enable("false"), .width(2)) multiplexer_7 (
    .in0(multiplexer_4_out), .in1(2'b01), .out(multiplexer_7_out), .sel(InitIn));
  Multiplexer #(.enable("false"), .width(2)) multiplexer_8 (
    .in0(multiplexer_5_out), .in1(2'b10), .out(multiplexer_8_out), .sel(InitIn));
  Way Way0 (
    .Tag(Tag), .Offset(Offset), .AgeIn(multiplexer_6_out), .WayWrite(WayWrite0), .Write(Write), .Value(Val0),
    .NewAge(NewAges), .BlockFromMem(BlockIn0), .Clk(ClkIn), .contain(contain0), .ByteReadOut(ByteReadOut0),
    .DirtyOut(DirtyWay0), .WayTagOut(WayTagOut0), .AgeOut(AgeWay0), .BlockOut(Block0));
  Way Way1 (
    .Tag(Tag), .Offset(Offset), .AgeIn(multiplexer_7_out), .WayWrite(WayWrite1), .Write(Write), .Value(Val1),
    .NewAge(NewAges), .BlockFromMem(BlockIn1), .Clk(ClkIn), .contain(contain1), .ByteReadOut(ByteReadOut1),
    .DirtyOut(DirtyWay1), .WayTagOut(WayTagOut1), .AgeOut(AgeWay1), .BlockOut(Block1));
  Way Way2 (
    .Tag(Tag), .Offset(Offset), .AgeIn(multiplexer_8_out), .WayWrite(WayWrite2), .Write(Write), .Value(Val2),
    .NewAge(NewAges), .BlockFromMem(BlockIn2), .Clk(ClkIn), .contain(contain2), .ByteReadOut(ByteReadOut2),
    .DirtyOut(DirtyWay2), .WayTagOut(WayTagOut2), .AgeOut(AgeWay2), .BlockOut(Block2));
  BitFinder #(.width(3)) bitfinder_1 (.in({contain2, contain1, contain0}), .index(WayContains), .found(contain));
  Multiplexer #(.enable("false"), .select(2), .width(8)) multiplexer_9 (
    .in0(ByteReadOut0), .in1(ByteReadOut1), .in2(ByteReadOut2), .out(ByteReadOut), .sel(WayContains));  // open: in3
  Comparator #(.mode("unsigned"), .width(2)) comparator_4 (
    .a(AgeWay0), .b(2'b10), .eq(comparator_4_eq[0]));  // open: gt, lt
  Comparator #(.mode("unsigned"), .width(2)) comparator_5 (
    .a(AgeWay1), .b(2'b10), .eq(comparator_4_eq[1]));  // open: gt, lt
  Comparator #(.mode("unsigned"), .width(2)) comparator_6 (
    .a(AgeWay2), .b(2'b10), .eq(comparator_4_eq[2]));  // open: gt, lt
  Comparator #(.mode("unsigned"), .width(7)) comparator_7 (
    .a(Tag), .b(WayTagOut0), .eq(comparator_7_eq[0]));  // open: gt, lt
  Comparator #(.mode("unsigned"), .width(7)) comparator_8 (
    .a(Tag), .b(WayTagOut1), .eq(comparator_7_eq[1]));  // open: gt, lt
  Comparator #(.mode("unsigned"), .width(7)) comparator_9 (
    .a(Tag), .b(WayTagOut2), .eq(comparator_7_eq[2]));  // open: gt, lt
  BitFinder #(.width(3)) bitfinder_2 (.in(comparator_4_eq), .index(OldWay));  // open: found
  BitFinder #(.width(3)) bitfinder_3 (.in(comparator_7_eq), .index(Match));  // open: found
  Multiplexer #(.enable("false"), .select(2), .width(32)) multiplexer_10 (
    .in0(Block0), .in1(Block1), .in2(Block2), .out(OlderBlockOut), .sel(OldWay));  // open: in3
  Multiplexer #(.enable("false"), .select(2)) multiplexer_11 (
    .in0(DirtyWay0), .in1(DirtyWay1), .in2(DirtyWay2), .out(OlderTagDirtyOut), .sel(OldWay));  // open: in3
  Multiplexer #(.enable("false"), .select(2), .width(7)) multiplexer_12 (
    .in0(WayTagOut0), .in1(WayTagOut1), .in2(WayTagOut2), .out(OlderTagOut), .sel(OldWay));  // open: in3

  // Other names for the same wires on the sheet: BlockIn[31:0] = BlockMem; clk = ClkIn; Initialize = InitIn;
  //   OlderBlock[31:0] = OlderBlockOut; Val[7:0] = Value; WayOlderDirty = OlderTagDirtyOut;
  //   WayTagOlder[6:0] = OlderTagOut
endmodule

module Way (
  input  [6:0] Tag,
  input  [1:0] Offset,
  input  [1:0] AgeIn,
  input  WayWrite,
  input  Write,
  input  [7:0] Value,
  input  NewAge,
  input  [31:0] BlockFromMem,
  input  Clk,
  output contain,
  output [7:0] ByteReadOut,
  output DirtyOut,
  output [6:0] WayTagOut,
  output [1:0] AgeOut,
  output [31:0] BlockOut
);

  wire comparator_1_eq, IsValid, multiplexer_1_out, multiplexer_2_out, multiplexer_3_out, multiplexer_4_out,
       multiplexer_5_out, WE0, WE1, WE2, WE3, WW0, WW1, WW2, WW3;
  wire [7:0] multiplexer_6_out, multiplexer_7_out, multiplexer_8_out, multiplexer_9_out;

  Demultiplexer #(.enable("false"), .select(2)) demultiplexer_1 (
    .out0(WW0), .out1(WW1), .out2(WW2), .out3(WW3), .in(WayWrite), .sel(Offset));
  Register #(.width(1)) register_1 (.D(1'b1), .en(WayWrite), .clk(Clk), .Q(IsValid));  // open: clr
  Multiplexer #(.enable("false")) multiplexer_1 (.in0(1'b0), .in1(1'b1), .out(multiplexer_1_out), .sel(Write));
  Register #(.width(2)) register_2 (.D(AgeIn), .en(NewAge), .clk(Clk), .Q(AgeOut));  // open: clr
  Register #(.width(7)) register_3 (.D(Tag), .en(WayWrite), .clk(Clk), .Q(WayTagOut));  // open: clr
  Register #(.width(1)) register_4 (.D(multiplexer_1_out), .en(WayWrite), .clk(Clk), .Q(DirtyOut));  // open: clr
  Multiplexer #(.enable("false")) multiplexer_2 (.in0(1'b1), .in1(WW0), .out(multiplexer_2_out), .sel(Write));
  Multiplexer #(.enable("false")) multiplexer_3 (.in0(1'b1), .in1(WW1), .out(multiplexer_3_out), .sel(Write));
  Multiplexer #(.enable("false")) multiplexer_4 (.in0(1'b1), .in1(WW2), .out(multiplexer_4_out), .sel(Write));
  Multiplexer #(.enable("false")) multiplexer_5 (.in0(1'b1), .in1(WW3), .out(multiplexer_5_out), .sel(Write));
  Multiplexer #(.enable("false"), .width(8)) multiplexer_6 (
    .in0(BlockFromMem[7:0]), .in1(Value), .out(multiplexer_6_out), .sel(Write));
  Multiplexer #(.enable("false"), .width(8)) multiplexer_7 (
    .in0(BlockFromMem[23:16]), .in1(Value), .out(multiplexer_7_out), .sel(Write));
  and and_1 (WE0, multiplexer_2_out, WayWrite);
  and and_2 (WE1, multiplexer_3_out, WayWrite);
  and and_3 (WE2, multiplexer_4_out, WayWrite);
  and and_4 (WE3, multiplexer_5_out, WayWrite);
  Register register_5 (.D(multiplexer_6_out), .en(WE0), .clk(Clk), .Q(BlockOut[7:0]));  // open: clr
  Register register_6 (.D(multiplexer_7_out), .en(WE2), .clk(Clk), .Q(BlockOut[23:16]));  // open: clr
  Multiplexer #(.enable("false"), .width(8)) multiplexer_8 (
    .in0(BlockFromMem[15:8]), .in1(Value), .out(multiplexer_8_out), .sel(Write));
  Multiplexer #(.enable("false"), .width(8)) multiplexer_9 (
    .in0(BlockFromMem[31:24]), .in1(Value), .out(multiplexer_9_out), .sel(Write));
  Multiplexer #(.enable("false"), .select(2), .width(8)) multiplexer_10 (
    .in0(BlockOut[7:0]), .in1(BlockOut[15:8]), .in2(BlockOut[23:16]), .in3(BlockOut[31:24]),
    .out(ByteReadOut), .sel(Offset));
  Register register_7 (.D(multiplexer_8_out), .en(WE1), .clk(Clk), .Q(BlockOut[15:8]));  // open: clr
  Register register_8 (.D(multiplexer_9_out), .en(WE3), .clk(Clk), .Q(BlockOut[31:24]));  // open: clr
  Comparator #(.width(7)) comparator_1 (.a(Tag), .b(WayTagOut), .eq(comparator_1_eq));  // open: gt, lt
  and and_5 (contain, comparator_1_eq, IsValid);

  // Other names for the same wires on the sheet: Age[1:0] = AgeOut; ByteMem0[7:0] = BlockFromMem[7:0];
  //   ByteMem1[7:0] = BlockFromMem[15:8]; ByteMem2[7:0] = BlockFromMem[23:16]; ByteMem3[7:0] = BlockFromMem[31:24];
  //   BlockToWrite[31:0] = BlockOut; Byte0[7:0] = BlockOut[7:0]; Byte1[7:0] = BlockOut[15:8];
  //   Byte2[7:0] = BlockOut[23:16]; Byte3[7:0] = BlockOut[31:24]; ByteRead[7:0] = ByteReadOut; Dirty = DirtyOut;
  //   Val[7:0] = Value; WayTag[6:0] = WayTagOut
endmodule
