// Logisim project adder4.circ as structural Verilog: 4 circuits, main circuit implementation
module implementation (
  input  [3:0] Ain,
  input  [3:0] Bin,
  input  Cinin,
  output [3:0] Sum_Out,
  output Carry_Out
);

  wire and_8_out, and_9_out, and_10_out, and_11_out, and_12_out, and_13_out, C0, C1, C2, E2, E3, E4, E5, G0,
       G1, G2, G3, P0, P1, P2, P3;

  and and_1 (G0, Ain[0], Bin[0]);
  and and_2 (G1, Ain[1], Bin[1]);
  and and_3 (G2, Ain[2], Bin[2]);
  and and_4 (G3, Ain[3], Bin[3]);
  xor xor_1 (P0, Ain[0], Bin[0]);
  xor xor_2 (P1, Ain[1], Bin[1]);
  xor xor_3 (P2, Ain[2], Bin[2]);
  xor xor_4 (P3, Ain[3], Bin[3]);
  and and_5 (E2, P3, G2);
  and and_6 (E3, P3, P2, G1);
  and and_7 (E4, P3, P2, P1, G0);
  and and_8 (and_8_out, P0, Cinin);
  and and_9 (and_9_out, P1, G0);
  and and_10 (and_10_out, P1, P0, Cinin);
  and and_11 (and_11_out, G1, P2);
  and and_12 (and_12_out, P2, G0, P1);
  and and_13 (and_13_out, P2, P1, P0, Cinin);
  and and_14 (E5, P3, P2, P1, P0, Cinin);
  or or_1 (C0, G0, and_8_out);
  or or_2 (C1, G1, and_9_out, and_10_out);
  or or_3 (C2, G2, and_11_out, and_12_out, and_13_out);
  or or_4 (Carry_Out, G3, E2, E3, E4, E5);
  Sum1 sum1_1 (.in_1(Ain[3]), .in_2(Bin[3]), .in_3(C2), .out_4(Sum_Out[3]));
  Sum1 sum1_2 (.in_1(Ain[2]), .in_2(Bin[2]), .in_3(C1), .out_4(Sum_Out[2]));
  Sum1 sum1_3 (.in_1(Ain[1]), .in_2(Bin[1]), .in_3(C0), .out_4(Sum_Out[1]));
  Sum1 sum1_4 (.in_1(Ain[0]), .in_2(Bin[0]), .in_3(Cinin), .out_4(Sum_Out[0]));

  // Other names for the same wires on the sheet: A[3:0] = Ain; A0 = Ain[0]; A1 = Ain[1]; A2 = Ain[2]; A3 = Ain[3];
  //   B[3:0] = Bin; B0 = Bin[0]; B1 = Bin[1]; B2 = Bin[2]; B3 = Bin[3]; C3 = Carry_Out; Cin = Cinin;
  //   Sum[3:0] = Sum_Out
endmodule

module G (
  input  in_1,
  input  in_2,
  output out_3
);

  and and_1 (out_3, in_1, in_2);
endmodule

module P (
  input  in_1,
  input  in_2,
  output out_3
);

  xor xor_1 (out_3, in_1, in_2);
endmodule

module Sum1 (
  input  in_1,
  input  in_2,
  input  in_3,
  output out_4
);

  xor xor_1 (out_4, in_1, in_2, in_3);
endmodule
