// Logisim project fun.circ as structural Verilog
module fun (
  input  x0,
  input  x1,
  input  x2,
  input  x3,
  output the_output
);

  wire and_1_out, and_2_out, not_1_out;

  and and_1 (and_1_out, x2, x3);
  and and_2 (and_2_out, x0, x1, not_1_out);
  not not_1 (not_1_out, and_1_out);
  or or_1 (the_output, and_2_out, and_1_out);

  // Notes on the sheet:
  //   (x0 * x1 * ~(x2 * x3)) + (x2 * x3)
endmodule
